// Digital circuit W01_E3.dig as structural Verilog
module W01_E3 (
  input  C,
  output out_1,
  output out_2
);

  _2x3bit_reg _2x3bit_reg_1 ();  // open: A, D, C, R0, R1
  _3_bit_ALU _3_bit_alu_1 ();  // open: In2, In1, Ctr, Out
  ROM #(.Bits(8)) rom_1 ();  // open: A, sel, D
  const_counter const_counter_1 ();  // open: out
  _8_bit_decoder _8_bit_decoder_1 ();  // open: In, Addr, Op2, Op1, Ctr

  // Notes on the sheet:
  //   contents of rom_1 (hex, n*v repeats v):
  //   e5
endmodule
