// Digital circuit 2x3bit_reg.dig as structural Verilog
module _2x3bit_reg (
  input  A,
  input  [2:0] D,
  input  C,
  output [2:0] R0,
  output [2:0] R1
);

  wire not_1_out;

  not not_1 (not_1_out, A);
  Register #(.Bits(3)) Reg0 (.D(D), .C(C), .en(not_1_out), .Q(R0));
  Register #(.Bits(3)) Reg1 (.D(D), .C(C), .en(A), .Q(R1));

  // Notes on the sheet:
  //   C: Hz: 2147483647
endmodule
