// Digital circuit 3_bit_ALU.dig as structural Verilog
module _3_bit_ALU (
  input  [2:0] In2,
  input  [2:0] In1,
  input  Ctr,
  output [2:0] Out
);

  wire and_1_out, not_1_out;
  wire [2:0] add_1_s, sub_1_s;

  and and_1 (and_1_out, Ctr, not_1_out);
  not not_1 (not_1_out, Ctr);
  Add #(.Bits(3)) add_1 (.a(In1), .b(In2), .c_i(and_1_out), .s(add_1_s));  // open: c_o
  Sub #(.Bits(3)) sub_1 (.a(In1), .b(In2), .c_i(and_1_out), .s(sub_1_s));  // open: c_o
  assign Out = ~Ctr ? add_1_s : 3'bz;  // DriverInvSel driverinvsel_1
  assign Out = Ctr ? sub_1_s : 3'bz;  // Driver driver_1
endmodule
