// Digital circuit 8_bit_decoder.dig as structural Verilog
module _8_bit_decoder (
  input  [7:0] In,
  output Addr,
  output [2:0] Op2,
  output [2:0] Op1,
  output Ctr
);


  assign Addr = In[0];
  assign Ctr = In[7];
  assign Op1 = In[6:4];
  assign Op2 = In[3:1];
endmodule
