// Digital circuit lab01_sub.dig as structural Verilog
module lab01_sub (
  input  C,
  output [2:0] R1,
  output [2:0] R0
);

  wire _8_bit_decoder_1_addr, _8_bit_decoder_1_ctr;
  wire [1:0] const_counter_1_out;
  wire [2:0] _3_bit_alu_1_out, _8_bit_decoder_1_op1, _8_bit_decoder_1_op2;
  wire [7:0] rom_1_d;

  const_counter const_counter_1 (.out(const_counter_1_out));
  ROM #(.Bits(8)) rom_1 (.A(const_counter_1_out), .sel(1'b1), .D(rom_1_d));
  _8_bit_decoder _8_bit_decoder_1 (
    .In(rom_1_d), .Addr(_8_bit_decoder_1_addr), .Op2(_8_bit_decoder_1_op2), .Op1(_8_bit_decoder_1_op1),
    .Ctr(_8_bit_decoder_1_ctr));
  _3_bit_ALU _3_bit_alu_1 (
    .In2(_8_bit_decoder_1_op2), .In1(_8_bit_decoder_1_op1), .Ctr(_8_bit_decoder_1_ctr), .Out(_3_bit_alu_1_out));
  _2x3bit_reg _2x3bit_reg_1 (.A(_8_bit_decoder_1_addr), .D(_3_bit_alu_1_out), .C(C), .R0(R0), .R1(R1));

  // Notes on the sheet:
  //   contents of rom_1 (hex, n*v repeats v):
  //   44
endmodule
