// Digital circuit lab02_sub.dig as structural Verilog
module lab02_sub (
  input  x,
  input  z,
  input  y,
  output x__not_z__plus__y__not_z
);

  wire and_1_out, and_2_out, not_1_out;

  not not_1 (not_1_out, z);
  and and_1 (and_1_out, x, not_1_out);
  and and_2 (and_2_out, not_1_out, y);
  or or_1 (x__not_z__plus__y__not_z, and_1_out, and_2_out);
endmodule
